# Fritzing sketch wemos_relay_webserver (saved by Fritzing 0.9.3b)

parts:
  v = AC Power [voltage=220 frequency=60]
  V1 = DC Power [voltage=5V]
  220v_to_5v = Transformer [package=transformer_smd]
  part = WeMos D1 Mini
  part_2 = WeMos D1 Mini Relay Shield

nets:
  N1: v.V+, 220v_to_5v.1
  5V: V1.V+, 220v_to_5v.4, part.5V, part_2.5V
  N2: V1.V-, 220v_to_5v.3, part.G, part_2.G
  GND: 220v_to_5v.2
  N3: part.D0, part.RST
  N4: part.D1, part_2.D1
